// Logisim project LabArq2.circ as structural Verilog: 10 circuits, main circuit main
module main (
);

  wire a, a1, a2, ac1_t, b, b1, b2, c, c1, c2, clk, clock_1_out, d, d1, d2, e, e1, e2, f, f1, f2, fin, g, g1,
       g2, Gano, niv0, niv1, niv2, Reset, x;
  wire [1:0] accion;
  wire [4:0] Ac1;
  wire [15:0] ca1, ca2, ca3, ca4, ca5, ca6, ca7, ca8, ca9, ca10, ca11, ca12, ca13, ca14, ca15, mov, random;

  Joystick #(.bits(2)) joystick_1 (.x(accion));  // open: y
  Button button_1 (.out(Reset));
  caidaEstrellas caidaestrellas_1 (
    .reset(Reset), .clk(clk), .random(random), .ca1(ca1), .ca2(ca2), .ca3(ca3), .ca4(ca4), .ca5(ca5),
    .ca6(ca6), .ca7(ca7), .ca8(ca8), .ca9(ca9), .ca10(ca10), .ca11(ca11), .ca12(ca12), .ca13(ca13),
    .ca14(ca14), .ca15(ca15));
  ContAciertos contaciertos_1 (
    .Entrada(Ac1), .g(g), .f(f), .a(a), .b(b), .g1(g1), .f1(f1), .a1(a1), .b1(b1), .e1(e1), .d1(d1), .c1(c1),
    .e(e), .d(d), .c(c));
  DotMatrix #(.dotshape("circle"), .inputtype("row"), .matrixcols(16), .matrixrows(16)) dotmatrix_1 (
    .row0(random), .row1(ca1), .row2(ca2), .row3(ca3), .row4(ca4), .row5(ca5), .row6(ca6), .row7(ca7),
    .row8(ca8), .row9(ca9), .row10(ca10), .row11(ca11), .row12(ca12), .row13(ca13), .row14(ca14), .row15(ca15));
  DotMatrix #(.dotshape("circle"), .inputtype("row"), .matrixcols(16), .matrixrows(1)) dotmatrix_2 (.row0(mov));
  Comparador comparador_1 (.conSup1(ca15), .conSup2(ca15), .conIn1(mov), .Fallos(x), .Aciertos(ac1_t));
  _7_Segment_Display u_7_segment_display_1 (.g(g), .f(f), .a(a), .b(b), .e(e), .d(d), .c(c));  // open: dp
  Clock clock_1 (.out(clock_1_out));
  _7_Segment_Display u_7_segment_display_2 (.g(g1), .f(f1), .a(a1), .b(b1), .e(e1), .d(d1), .c(c1));  // open: dp
  LED led_1 (.in(fin));
  LED led_2 (.in(Gano));
  Movimiento movimiento_1 (.Reset(Reset), .in_2(accion), .salida(mov));
  _7_Segment_Display u_7_segment_display_3 (.g(g2), .f(f2), .a(a2), .b(b2), .e(e2), .d(d2), .c(c2));  // open: dp
  DivFrec divfrec_1 (
    .reset(Reset), .Clock(clock_1_out), .fin(fin), .nivel2(niv2), .nivel1(niv1), .nivel0(niv0),
    .frecFinal(clk));  // open: CLKD2, CLKD4, CLKD8
  ContadorFallas contadorfallas_1 (
    .x(x), .reset(Reset), .Clock(clk), .z(fin), .g(g2), .f(f2), .a(a2), .b(b2), .e(e2), .d(d2), .c(c2));  // open: cte
  Aciertos aciertos_1 (.reset(Reset), .entrada(ac1_t), .SalAciertos(Ac1));
  Niveles niveles_1 (.entrada(Ac1), .nivel1(niv1), .nivel0(niv0), .nivel2(niv2), .gano(Gano));

  // Notes on the sheet:
  //   MOVER
  //   INICIAR DE NUEVO
  //   CANTIDAD  DE ACIERTOS
  //   FIN DE LA PARTIDA
  //   HAZ GANADO
  //   CANTIDAD DE FALLOS
endmodule

module random01 (
  input  reset,
  input  in_2,
  output [15:0] out_3
);

  wire [3:0] random_1_out;

  Random #(.width(4)) random_1 (.clr(reset), .clk(in_2), .out(random_1_out));  // open: next
  Decoder #(.select(4)) decoder_1 (
    .out0(out_3[0]), .out1(out_3[1]), .out2(out_3[2]), .out3(out_3[3]), .out4(out_3[4]), .out5(out_3[5]),
    .out6(out_3[6]), .out7(out_3[7]), .out8(out_3[8]), .out9(out_3[9]), .out10(out_3[10]), .out11(out_3[11]),
    .out12(out_3[12]), .out13(out_3[13]), .out14(out_3[14]), .out15(out_3[15]), .sel(random_1_out));  // open: en
endmodule

module ContAciertos (
  input  [4:0] Entrada,
  output g,
  output f,
  output a,
  output b,
  output g1,
  output f1,
  output a1,
  output b1,
  output e1,
  output d1,
  output c1,
  output e,
  output d,
  output c
);

  wire binairy_to_bcd_converter_1_p2, binairy_to_bcd_converter_1_p3;

  // Binairy_to_BCD_converter #(.binvalue(5)) binairy_to_bcd_converter_1: pin names not known; wires that end beside it: Entrada, binairy_to_bcd_converter_1_p2, binairy_to_bcd_converter_1_p3
  // BCD_to_7_Segment_decoder bcd_to_7_segment_decoder_1: pin names not known; wires that end beside it: g, e, f, d, binairy_to_bcd_converter_1_p2, a, c, b
  // BCD_to_7_Segment_decoder bcd_to_7_segment_decoder_2: pin names not known; wires that end beside it: g1, e1, f1, d1, binairy_to_bcd_converter_1_p3, a1, c1, b1
endmodule

module Comparador (
  input  [15:0] conSup1,
  input  [15:0] conSup2,
  input  [15:0] conIn1,
  output Fallos,
  output Aciertos
);

  wire comparator_2_eq, not_1_out, not_2_out;

  Comparator #(.width(16)) comparator_1 (.a(conSup2), .b(conIn1), .eq(Aciertos));  // open: gt, lt
  not not_1 (not_1_out, comparator_2_eq);
  Comparator #(.width(16)) comparator_2 (.a(conSup1), .b({16{1'b0}}), .eq(comparator_2_eq));  // open: gt, lt
  not not_2 (not_2_out, Aciertos);
  and and_1 (Fallos, not_1_out, not_2_out);
endmodule

module Aciertos (
  input  reset,
  input  entrada,
  output [4:0] SalAciertos
);

  Counter #(.max('h1f), .width(5)) counter_1 (
    .clr(reset), .up(1'b1), .count(1'b1), .clk(entrada), .Q(SalAciertos));  // open: load, D, carry
endmodule

module Movimiento (
  input  Reset,
  input  [1:0] in_2,
  output [15:0] salida
);

  wire clock_1_out, clock_2_out;
  wire [3:0] counter_2_q, VALUE;

  Clock clock_1 (.out(clock_1_out));
  Counter #(.max('hf), .width(4)) counter_1 (
    .clr(Reset), .up(1'b1), .count(1'b1), .clk(clock_1_out), .Q(VALUE));  // open: load, D, carry
  Clock clock_2 (.out(clock_2_out));
  Counter #(.max('hf), .ongoal("stay"), .width(4)) counter_2 (
    .clr(Reset), .up(in_2[1]), .count(in_2[0]), .clk(clock_2_out), .Q(counter_2_q));  // open: load, D, carry
  Decoder #(.select(4)) decoder_1 (
    .out0(salida[15]), .out1(salida[14]), .out2(salida[13]), .out3(salida[12]), .out4(salida[11]),
    .out5(salida[10]), .out6(salida[9]), .out7(salida[8]), .out8(salida[7]), .out9(salida[6]),
    .out10(salida[5]), .out11(salida[4]), .out12(salida[3]), .out13(salida[2]), .out14(salida[1]),
    .out15(salida[0]), .sel(counter_2_q));  // open: en

  // Other names for the same wires on the sheet: r = Reset
endmodule

module ContadorFallas (
  input  x,
  input  reset,
  input  Clock,
  input  cte,
  output z,
  output g,
  output f,
  output a,
  output b,
  output e,
  output d,
  output c
);

  wire binairy_to_bcd_converter_1_p2, J1, J2, K1, K2, Q0, Q1, Q2;

  and and_1 (J2, Q1, Q0, x);
  and and_2 (K2, Q1, Q0, x);
  and and_3 (J1, Q0, x);
  and and_4 (K1, Q0, x);
  and and_5 (z, Q2, Q1, Q0);
  // Binairy_to_BCD_converter #(.binvalue(4)) binairy_to_bcd_converter_1: pin names not known; wires that end beside it: {cte, Q2, Q1, Q0}, binairy_to_bcd_converter_1_p2
  // BCD_to_7_Segment_decoder bcd_to_7_segment_decoder_1: pin names not known; wires that end beside it: g, e, f, d, binairy_to_bcd_converter_1_p2, a, c, b
  J_K_Flip_Flop J2K2 (.J(J2), .K(K2), .clk(Clock), .Q(Q2), .reset(reset));  // open: Qn, preset
  J_K_Flip_Flop J1K1 (.J(J1), .K(K1), .clk(Clock), .Q(Q1), .reset(reset));  // open: Qn, preset
  J_K_Flip_Flop J0K0 (.J(x), .K(x), .clk(Clock), .Q(Q0), .reset(reset));  // open: Qn, preset

  // Other names for the same wires on the sheet: J0 = x; K0 = x; r = reset
endmodule

module DivFrec (
  input  reset,
  input  Clock,
  input  fin,
  input  nivel2,
  input  nivel1,
  input  nivel0,
  output CLKD2,
  output CLKD4,
  output frecFinal,
  output CLKD8
);

  wire and_1_out, not_1_out;
  wire [2:0] VALUE;

  not not_1 (not_1_out, fin);
  and and_1 (and_1_out, Clock, not_1_out);
  Counter #(.max('h7), .width(3)) counter_1 (
    .clr(reset), .up(1'b1), .count(1'b1), .clk(and_1_out), .Q(VALUE));  // open: load, D, carry
  and and_2 (CLKD2, nivel2, VALUE[0]);
  and and_3 (CLKD4, VALUE[0], VALUE[1], nivel1);
  and and_4 (CLKD8, VALUE[0], VALUE[1], VALUE[2], nivel0);
  or or_1 (frecFinal, CLKD2, CLKD4, CLKD8);
endmodule

module caidaEstrellas (
  input  reset,
  input  clk,
  output [15:0] random,
  output [15:0] ca1,
  output [15:0] ca2,
  output [15:0] ca3,
  output [15:0] ca4,
  output [15:0] ca5,
  output [15:0] ca6,
  output [15:0] ca7,
  output [15:0] ca8,
  output [15:0] ca9,
  output [15:0] ca10,
  output [15:0] ca11,
  output [15:0] ca12,
  output [15:0] ca13,
  output [15:0] ca14,
  output [15:0] ca15
);

  random01 random01_1 (.reset(reset), .in_2(clk), .out_3(random));
  // Shift_Register #(.length(15), .width(16)) shift_register_1: pin names not known; wires that end beside it: reset, random, clk, ca1, ca2, ca3, ca4, ca5, ca6, ca7, ca8, ca9, ca10, ca11, ca12
endmodule

module Niveles (
  input  [4:0] entrada,
  output nivel1,
  output nivel0,
  output nivel2,
  output gano
);

  wire comparator_1_gt, comparator_2_eq, comparator_3_lt, comparator_4_gt, comparator_5_gt, comparator_6_lt,
       not_1_out, or_1_out;

  Comparator #(.mode("unsigned"), .width(5)) comparator_1 (
    .a(entrada), .b({5{1'b0}}), .gt(comparator_1_gt));  // open: eq, lt
  Comparator #(.mode("unsigned"), .width(5)) comparator_2 (
    .a(entrada), .b({5{1'b0}}), .eq(comparator_2_eq));  // open: gt, lt
  Comparator #(.mode("unsigned"), .width(5)) comparator_3 (
    .a(entrada), .b(5'b00101), .lt(comparator_3_lt));  // open: gt, eq
  Comparator #(.mode("unsigned"), .width(5)) comparator_4 (
    .a(entrada), .b(5'b01001), .gt(comparator_4_gt));  // open: eq, lt
  Comparator #(.mode("unsigned"), .width(5)) comparator_5 (
    .a(entrada), .b(5'b00100), .gt(comparator_5_gt));  // open: eq, lt
  not not_1 (not_1_out, comparator_4_gt);
  Comparator #(.mode("unsigned"), .width(5)) comparator_6 (
    .a(entrada), .b(5'b10100), .lt(comparator_6_lt));  // open: gt, eq
  or or_1 (or_1_out, comparator_1_gt, comparator_2_eq);
  and and_1 (nivel2, comparator_4_gt, comparator_6_lt);
  Comparator #(.mode("unsigned"), .width(5)) comparator_7 (.a(entrada), .b(5'b10100), .eq(gano));  // open: gt, lt
  and and_2 (nivel1, not_1_out, comparator_5_gt);
  and and_3 (nivel0, or_1_out, comparator_3_lt);
endmodule
